# Fritzing sketch board (saved by Fritzing 0.9.3b)
breadboards: 1

parts:
  R1 = Resistor [tolerance=±5% resistance=220 package=THT]
  S1 = Pushbutton [package="[THT]"]
  LED1 = LED - 5mm [color="Red (633nm)" package="5 mm [THT]"]  # not connected
  Part1 = Arduino Nano (Rev3.0)

nets:
  N1: R1.Pin_0, Part1.D13/SCK
  N2: S1.Pin_1, S1.Pin_2, Part1.GND
  N3: S1.Pin_3, S1.Pin_4, Part1.D2
