# Fritzing sketch board (saved by Fritzing 0.9.3b)
breadboards: 1

parts:
  Part1 = Arduino Nano (Rev3.0)
  J1 = Basic Servo
  hc-sr1 = hc-sr04

nets:
  GND: Part1.GND, J1.gnd, hc-sr1.GND
  N1: Part1.D5, J1.pulse
  N2: Part1.D6, hc-sr1.Trig
  N3: Part1.D7, hc-sr1.Echo
  VCC: Part1.5V, J1.vcc, hc-sr1.VCC
